// Logisim project fulladder_2.circ as structural Verilog: 1 circuit, main circuit main
module main (
  input  CARRY_IN,
  input  A,
  input  B,
  output SUM,
  output out_5
);

  wire and_1_out, and_2_out, xor_1_out;

  xor xor_1 (xor_1_out, A, B);
  and and_1 (and_1_out, B, A);
  xor xor_2 (SUM, CARRY_IN, xor_1_out);
  and and_2 (and_2_out, xor_1_out, CARRY_IN);
  or or_1 (out_5, and_2_out, and_1_out);

  // Notes on the sheet:
  //   HALF ADDER 1
  //   HALF ADDER 2
  //   CARRY OUT
endmodule
