// Logisim project fulladder_3.circ as structural Verilog: 2 circuits, main circuit main
module main (
  input  carry_in,
  input  a,
  input  b,
  output sum,
  output carry_out
);

  wire halfadder_1_out_3, halfadder_1_out_4, halfadder_2_out_4;

  HALFADDER halfadder_1 (.in_1(a), .in_2(b), .out_3(halfadder_1_out_3), .out_4(halfadder_1_out_4));
  HALFADDER halfadder_2 (.in_1(carry_in), .in_2(halfadder_1_out_3), .out_3(sum), .out_4(halfadder_2_out_4));
  or or_1 (carry_out, halfadder_2_out_4, halfadder_1_out_4);

  // Notes on the sheet:
  //   half adder
  //   half adder
endmodule

module HALFADDER (
  input  in_1,
  input  in_2,
  output out_3,
  output out_4
);

  xor xor_1 (out_3, in_1, in_2);
  and and_1 (out_4, in_1, in_2);
endmodule
