// Logisim project halfadder_nand.circ as structural Verilog: 1 circuit, main circuit main
module main (
  input  A,
  input  B,
  output SUM,
  output CARYY_OUT
);

  wire nand_1_out, nand_2_out, nand_3_out;

  nand nand_1 (nand_1_out, A, B);
  nand nand_2 (nand_2_out, A, nand_1_out);
  nand nand_3 (nand_3_out, nand_1_out, B);
  nand nand_4 (SUM, nand_2_out, nand_3_out);
  nand nand_5 (CARYY_OUT, nand_1_out, nand_1_out);

  // Notes on the sheet:
  //   HALF ADDER USING ONLY NAND GATES
endmodule
