// Logisim project halfadder_nor.circ as structural Verilog: 1 circuit, main circuit main
module main (
  input  A,
  input  B,
  output SUM,
  output CARRY_OUT
);

  wire nor_1_out, nor_2_out, nor_3_out;

  nor nor_1 (nor_1_out, B, A);
  nor nor_2 (nor_2_out, A, A);
  nor nor_3 (nor_3_out, B, B);
  nor nor_4 (CARRY_OUT, nor_2_out, nor_3_out);
  nor nor_5 (SUM, nor_1_out, CARRY_OUT);

  // Notes on the sheet:
  //   output = ~A~B
  //   HALF ADDER USING ONLY NOR GATES
  //   output = AB
  //   (A + B) (~A + ~B)
endmodule
