// Logisim project 6a.circ as structural Verilog: 1 circuit, main circuit main
module main (
  input  in_1,
  input  in_2,
  input  in_3,
  output out_4
);

  wire A_B_C_out, A_B_C_prime_out, A_B_out, A_B_prime_C_out, A_B_prime_out, A_prime_B_C_out, A_prime_B_out,
       not_1_out, not_2_out, not_3_out, or_1_out, or_2_out;

  not not_1 (not_1_out, in_1);
  not not_2 (not_2_out, in_2);
  not not_3 (not_3_out, in_3);
  and A_prime_B (A_prime_B_out, not_1_out, in_2, in_2);
  and A_B_prime (A_B_prime_out, in_1, not_2_out);
  and A_B (A_B_out, in_1, in_2);
  and A_prime_B_C (A_prime_B_C_out, A_prime_B_out, in_3);
  and A_B_prime_C (A_B_prime_C_out, A_B_prime_out, in_3);
  and A_B_C (A_B_C_out, A_B_out, in_3);
  and A_B_C_prime (A_B_C_prime_out, A_B_out, not_3_out);
  or or_1 (or_1_out, A_prime_B_C_out, A_B_prime_C_out);
  or or_2 (or_2_out, A_B_C_out, A_B_C_prime_out);
  or or_3 (out_4, or_1_out, or_2_out);

  // Notes on the sheet:
  //   B
  //   A
  //   C
  //   GIVEN EXPRESSION : A' B C + A B' C + A B C' + A B C
  //   A' B C + A B' C
  //   A B C + A B C'
  //   A' B C + A B' C + A B C' + A B C
endmodule
