// Logisim project 6b.circ as structural Verilog: 1 circuit, main circuit main
module main (
  input  in_1,
  input  in_2,
  input  in_3,
  output out_4
);

  wire A_B_out, B_C_out, C_A_out, or_1_out;

  and A_B (A_B_out, in_1, in_2);
  and B_C (B_C_out, in_2, in_2, in_3);
  and C_A (C_A_out, in_1, in_3);
  or or_1 (or_1_out, A_B_out, B_C_out);
  or or_2 (out_4, or_1_out, C_A_out);

  // Notes on the sheet:
  //   B
  //   A
  //   C
  //   SIMPLIFIED EXPRESSION - A B + BC + CA
  //   A B + B C
  //   A B + B C + C A
endmodule
