// Logisim project multiplexer.circ as structural Verilog: 1 circuit, main circuit main
module main (
  input  I0,
  input  I1,
  input  I2,
  input  I3,
  input  I4,
  input  in_6,
  input  I5,
  input  I6,
  input  I7,
  input  S2,
  input  S1,
  input  S0,
  output out_13
);

  wire and_1_out, and_2_out, and_3_out, and_4_out, and_5_out, and_6_out, and_7_out, and_8_out, not_1_out,
       not_2_out, not_3_out, or_1_out;

  not not_1 (not_1_out, S2);
  not not_2 (not_2_out, S1);
  not not_3 (not_3_out, S0);
  and and_1 (and_1_out, I0, not_1_out, not_2_out, not_3_out);
  and and_2 (and_2_out, I1, not_1_out, not_2_out, S0);
  and and_3 (and_3_out, I2, not_1_out, S1, not_3_out);
  and and_4 (and_4_out, I3, not_1_out, S1, S0);
  and and_5 (and_5_out, I4, S2, not_2_out, not_3_out);
  and and_6 (and_6_out, I5, S2, not_2_out, S0);
  and and_7 (and_7_out, I6, S2, S1, not_3_out);
  and and_8 (and_8_out, I7, S2, S1, S0);
  or or_1 (or_1_out, and_1_out, and_2_out, and_3_out, and_4_out, and_5_out, and_6_out, and_7_out, and_8_out);
  and and_9 (out_13, or_1_out, in_6);

  // Notes on the sheet:
  //   8 * 1 MULTIPLEXER
  //   Enable
  //   Y
endmodule
