// Logisim project flipflops.circ as structural Verilog: 1 circuit, main circuit main
module main (
  input  S,
  input  R,
  input  in_3,
  input  J,
  input  in_5,
  input  in_6,
  input  K,
  input  T,
  input  in_9,
  input  in_10,
  input  in_11,
  input  in_12,
  output Q,
  output Q_prime,
  output Q_2,
  output Q_prime_2,
  output Q_3,
  output out_18,
  output Q_prime_3,
  output Q_4,
  output out_21,
  output Q_prime_4,
  output Q_5,
  output Q_prime_5,
  output Q_6,
  output Q_prime_6
);

  wire clock_1_out, clock_2_out, clock_3_out, clock_4_out, clock_5_out, clock_6_out, clock_7_out,
       clock_8_out, nand_1_out, nand_2_out, nand_3_out, nand_4_out, nand_5_out, nand_6_out, nand_7_out,
       nand_8_out, nand_9_out, nand_10_out, nand_11_out, nand_12_out, nand_13_out, nand_14_out, nand_15_out,
       nand_16_out, nand_25_out, nand_26_out, nand_27_out, nand_28_out, not_1_out, not_2_out, not_3_out;

  Clock clock_1 (.out(clock_1_out));
  Clock clock_2 (.out(clock_2_out));
  not not_1 (not_1_out, in_3);
  Clock clock_3 (.out(clock_3_out));
  Clock clock_4 (.out(clock_4_out));
  Clock clock_5 (.out(clock_5_out));
  Clock clock_6 (.out(clock_6_out));
  nand nand_1 (nand_1_out, Q_prime_5, in_10, clock_1_out);
  nand nand_2 (nand_2_out, clock_1_out, in_11, Q_5);
  nand nand_3 (nand_3_out, Q_prime_6, in_12, clock_2_out);
  nand nand_4 (nand_4_out, clock_2_out, in_12, Q_6);
  nand nand_5 (nand_5_out, S, clock_3_out);
  nand nand_6 (nand_6_out, clock_3_out, R);
  nand nand_7 (nand_7_out, in_3, clock_4_out);
  nand nand_8 (nand_8_out, clock_4_out, not_1_out);
  nand nand_9 (nand_9_out, Q_prime_3, J, clock_5_out);
  nand nand_10 (nand_10_out, clock_5_out, K, Q_3);
  nand nand_11 (nand_11_out, Q_prime_4, T, clock_6_out);
  nand nand_12 (nand_12_out, clock_6_out, T, Q_4);
  not not_2 (not_2_out, clock_1_out);
  not not_3 (not_3_out, clock_2_out);
  nand nand_13 (nand_13_out, nand_1_out, nand_14_out);
  nand nand_14 (nand_14_out, nand_13_out, nand_2_out);
  nand nand_15 (nand_15_out, nand_3_out, nand_16_out);
  nand nand_16 (nand_16_out, nand_15_out, nand_4_out);
  nand nand_17 (Q, nand_5_out, Q_prime);
  nand nand_18 (Q_prime, Q, nand_6_out);
  nand nand_19 (Q_2, nand_7_out, Q_prime_2);
  nand nand_20 (Q_prime_2, Q_2, nand_8_out);
  not nand_21 (Q_3, nand_9_out);  // NAND_Gate
  nand nand_22 (Q_prime_3, Q_3, nand_10_out);
  nand nand_23 (Q_4, nand_11_out, Q_prime_4);
  nand nand_24 (Q_prime_4, Q_4, nand_12_out);
  nand nand_25 (nand_25_out, nand_13_out, not_2_out);
  nand nand_26 (nand_26_out, not_2_out, nand_14_out);
  nand nand_27 (nand_27_out, nand_15_out, not_3_out);
  nand nand_28 (nand_28_out, not_3_out, nand_16_out);
  Clock clock_7 (.out(clock_7_out));
  J_K_Flip_Flop j_k_ff_1 (.J(in_5), .clk(clock_8_out), .K(in_6), .Q(out_18));  // open: Qn, preset, en, reset
  Clock clock_8 (.out(clock_8_out));
  T_Flip_Flop t_ff_1 (.clk(clock_7_out), .T(in_9), .Q(out_21));  // open: Qn, preset, reset, en
  nand nand_29 (Q_5, nand_25_out, Q_prime_5);
  nand nand_30 (Q_prime_5, Q_5, nand_26_out);
  nand nand_31 (Q_6, nand_27_out, Q_prime_6);
  nand nand_32 (Q_prime_6, Q_6, nand_28_out);

  // Notes on the sheet:
  //   CLK
  //   CLK
  //   CLK
  //   CLK
  //   SR FLIP FLOP
  //   D FLIP FLOP
  //   JK FLIP FLOP
  //   T FLIP FLOP
  //   JK FLIP FLOP
  //   T FLIP FLOP
  //   T FLIP FLOP
endmodule
