// Logisim project registers.circ as structural Verilog: 1 circuit, main circuit main
module main (
  input  INPUT,
  input  INPUT_2,
  input  in_3,
  input  in_4,
  input  in_5,
  input  in_6,
  input  D3,
  input  D2,
  input  D1,
  input  D0,
  input  nLOAD,
  output out_12,
  output out_13,
  output out_14,
  output out_15,
  output out_16,
  output out_17,
  output out_18,
  output out_19,
  output out_20,
  output out_21
);

  wire and_1_out, and_2_out, and_3_out, and_4_out, and_5_out, and_6_out, clock_1_out, clock_2_out,
       clock_3_out, clock_4_out, d_ff_1_q, d_ff_2_q, d_ff_5_q, d_ff_8_q, d_ff_9_q, d_ff_15_q, not_1_out,
       or_1_out, or_2_out, or_3_out;

  Clock clock_1 (.out(clock_1_out));
  Clock clock_2 (.out(clock_2_out));
  Clock clock_3 (.out(clock_3_out));
  Clock clock_4 (.out(clock_4_out));
  not not_1 (not_1_out, nLOAD);
  D_Flip_Flop d_ff_1 (.clk(clock_1_out), .D(D3), .Q(d_ff_1_q));  // open: Qn, preset, en, reset
  D_Flip_Flop d_ff_2 (.clk(clock_2_out), .D(INPUT), .Q(d_ff_2_q));  // open: Qn, preset, en, reset
  D_Flip_Flop d_ff_3 (.clk(clock_3_out), .D(INPUT_2), .Q(out_13));  // open: Qn, preset, en, reset
  D_Flip_Flop d_ff_4 (.clk(clock_4_out), .D(in_3), .Q(out_17));  // open: Qn, preset, en, reset
  and and_1 (and_1_out, d_ff_1_q, nLOAD);
  and and_2 (and_2_out, not_1_out, D2);
  or or_1 (or_1_out, and_1_out, and_2_out);
  D_Flip_Flop d_ff_5 (.clk(clock_2_out), .D(d_ff_2_q), .Q(d_ff_5_q));  // open: Qn, preset, en, reset
  D_Flip_Flop d_ff_6 (.clk(clock_3_out), .D(out_13), .Q(out_14));  // open: Qn, preset, en, reset
  D_Flip_Flop d_ff_7 (.clk(clock_4_out), .D(in_4), .Q(out_18));  // open: Qn, preset, en, reset
  D_Flip_Flop d_ff_8 (.clk(clock_1_out), .D(or_1_out), .Q(d_ff_8_q));  // open: Qn, preset, en, reset
  and and_3 (and_3_out, d_ff_8_q, nLOAD);
  D_Flip_Flop d_ff_9 (.clk(clock_2_out), .D(d_ff_5_q), .Q(d_ff_9_q));  // open: Qn, preset, en, reset
  D_Flip_Flop d_ff_10 (.clk(clock_3_out), .D(out_14), .Q(out_15));  // open: Qn, preset, en, reset
  D_Flip_Flop d_ff_11 (.clk(clock_4_out), .D(in_5), .Q(out_19));  // open: Qn, preset, en, reset
  and and_4 (and_4_out, not_1_out, D1);
  or or_2 (or_2_out, and_3_out, and_4_out);
  D_Flip_Flop d_ff_12 (.clk(clock_2_out), .D(d_ff_9_q), .Q(out_12));  // open: Qn, preset, en, reset
  D_Flip_Flop d_ff_13 (.clk(clock_3_out), .D(out_15), .Q(out_16));  // open: Qn, preset, en, reset
  D_Flip_Flop d_ff_14 (.clk(clock_4_out), .D(in_6), .Q(out_20));  // open: Qn, preset, en, reset
  D_Flip_Flop d_ff_15 (.clk(clock_1_out), .D(or_2_out), .Q(d_ff_15_q));  // open: Qn, preset, en, reset
  and and_5 (and_5_out, d_ff_15_q, nLOAD);
  or or_3 (or_3_out, and_5_out, and_6_out);
  and and_6 (and_6_out, not_1_out, D0);
  D_Flip_Flop d_ff_16 (.clk(clock_1_out), .D(or_3_out), .Q(out_21));  // open: Qn, preset, en, reset

  // Notes on the sheet:
  //   SHIFT
  //   CLK
  //   CLK
  //   CLK
  //   4 BIT - SERIAL IN SERIAL OUT SHIFT REGISTER
  //   4 BIT - SERIAL IN PARALLEL OUT SHIFT REGISTER
  //   4 BIT PARALLEL IN PARALLEL OUT SHIFT REGISTER
  //   4 BIT PARALLEL INPUT SERIAL OUTPUT SHIFT REGISTER
endmodule
