// Logisim project 3-bit synchronous using D.circ as structural Verilog: 1 circuit, main circuit main
module main (
  output lsb,
  output out_2,
  output msb,
  output lsb_2,
  output out_5,
  output msb_2
);

  wire and_1_out, and_2_out, and_3_out, and_4_out, and_5_out, and_6_out, button_1_out, button_2_out,
       clock_1_out, clock_2_out, d_ff_1_qn, d_ff_2_q, d_ff_3_qn, d_ff_4_q, d_ff_5_qn, d_ff_6_q, or_1_out,
       or_2_out, xor_1_out, xor_2_out;

  Clock clock_1 (.out(clock_1_out));
  Button button_1 (.out(button_1_out));
  Clock clock_2 (.out(clock_2_out));
  Button button_2 (.out(button_2_out));
  D_Flip_Flop #(.trigger("falling")) d_ff_1 (
    .clk(clock_1_out), .D(d_ff_1_qn), .Q(lsb), .Qn(d_ff_1_qn), .reset(button_1_out));  // open: preset, en
  D_Flip_Flop #(.trigger("falling")) d_ff_2 (
    .clk(clock_2_out), .D(lsb_2), .Q(d_ff_2_q), .Qn(lsb_2), .reset(button_2_out));  // open: preset, en
  xor xor_1 (xor_1_out, lsb, out_2);
  xor xor_2 (xor_2_out, d_ff_2_q, d_ff_4_q);
  D_Flip_Flop #(.trigger("falling")) d_ff_3 (
    .clk(clock_1_out), .D(xor_1_out), .Q(out_2), .Qn(d_ff_3_qn), .reset(button_1_out));  // open: preset, en
  D_Flip_Flop #(.trigger("falling")) d_ff_4 (
    .clk(clock_2_out), .D(xor_2_out), .Q(d_ff_4_q), .Qn(out_5), .reset(button_2_out));  // open: preset, en
  and and_1 (and_1_out, d_ff_1_qn, msb);
  and and_2 (and_2_out, lsb_2, d_ff_6_q);
  or or_1 (or_1_out, and_1_out, and_4_out, and_3_out);
  and and_3 (and_3_out, lsb, out_2, d_ff_5_qn);
  and and_4 (and_4_out, d_ff_3_qn, msb);
  or or_2 (or_2_out, and_2_out, and_5_out, and_6_out);
  and and_5 (and_5_out, out_5, d_ff_6_q);
  D_Flip_Flop #(.trigger("falling")) d_ff_5 (
    .clk(clock_1_out), .D(or_1_out), .Q(msb), .Qn(d_ff_5_qn), .reset(button_1_out));  // open: preset, en
  D_Flip_Flop #(.trigger("falling")) d_ff_6 (
    .clk(clock_2_out), .D(or_2_out), .Q(d_ff_6_q), .Qn(msb_2), .reset(button_2_out));  // open: preset, en
  and and_6 (and_6_out, d_ff_2_q, d_ff_4_q, msb_2);

  // Notes on the sheet:
  //   MOD - 8 SYNCHRONOUS UP COUNTER
  //   MOD - 8 SYNCHRONOUS DOWN COUNTER
  //   Da = ~Qa
  //   Db = Qb~Qa + Qa~Qb
  //   Dc = Qc~Qa + Qc~Qb + QaQb~Qc
endmodule
