// Logisim project 3bit-ripple.circ as structural Verilog: 1 circuit, main circuit main
module main (
  output lsb,
  output out_2,
  output msb,
  output out_4,
  output out_5,
  output out_6
);

  wire button_1_out, button_2_out, clock_1_out, clock_2_out, j_k_ff_2_q, j_k_ff_4_q;

  Clock clock_1 (.out(clock_1_out));
  Button button_1 (.out(button_1_out));
  Clock clock_2 (.out(clock_2_out));
  Button button_2 (.out(button_2_out));
  J_K_Flip_Flop #(.trigger("falling")) j_k_ff_1 (
    .J(1'b1), .clk(clock_1_out), .K(1'b1), .Q(lsb), .reset(button_1_out));  // open: Qn, preset, en
  J_K_Flip_Flop #(.trigger("falling")) j_k_ff_2 (
    .J(1'b1), .clk(clock_2_out), .K(1'b1), .Q(j_k_ff_2_q), .Qn(out_4));  // open: preset, en, reset
  J_K_Flip_Flop #(.trigger("falling")) j_k_ff_3 (
    .J(1'b1), .clk(lsb), .K(1'b1), .Q(out_2), .reset(button_1_out));  // open: Qn, preset, en
  J_K_Flip_Flop #(.trigger("falling")) j_k_ff_4 (
    .J(1'b1), .clk(j_k_ff_2_q), .K(1'b1), .Q(j_k_ff_4_q), .Qn(out_5));  // open: preset, en, reset
  J_K_Flip_Flop #(.trigger("falling")) j_k_ff_5 (
    .J(1'b1), .clk(out_2), .K(1'b1), .Q(msb), .reset(button_1_out));  // open: Qn, preset, en
  J_K_Flip_Flop #(.trigger("falling")) j_k_ff_6 (
    .J(1'b1), .clk(j_k_ff_4_q), .K(1'b1), .Qn(out_6), .reset(button_2_out));  // open: Q, preset, en

  // Notes on the sheet:
  //   clk
  //   clk
  //   lsb
  //   3 bit-up Ripple counter
  //   3 bit down ripple counter
  //   msb
endmodule
